# Fritzing sketch wiring-diagram (saved by Fritzing 0.9.1b)
breadboards: 1

parts:
  S1 = Round Pushbutton
  Raspberry_Pi1 = Raspberry Pi B rev2
  LED1 = LED - 5mm [color="Red (633nm)" package="5 mm [THT]"]
  LED2 = LED - 5mm [color="Blue (505nm)" package="5 mm [THT]"]
  LED3 = LED - 5mm [color="Yellow (592nm)" package="5 mm [THT]"]
  LED4 = LED - 5mm [color="Green (565nm)" package="5 mm [THT]"]
  S2 = Pushbutton [package=THT]
  R1 = Resistor [tolerance=±5% resistance=220 package=THT]
  LED5 = LED - 5mm [color="White (6500K)" package="5 mm [THT]"]
  S3 = Toggle Switch [package=THT]

nets:
  N1: S1.leg0, Raspberry_Pi1.GPIO_27
  N2: S1.leg1, Raspberry_Pi1.GND, S2.leg0, R1.Pin_0
  N3: Raspberry_Pi1.3V3, S3.L1
  N4: Raspberry_Pi1.GPIO_23, S2.leg1
  N5: Raspberry_Pi1.GPIO_17, LED5.anode
  N6: Raspberry_Pi1.GPIO_18, LED2.anode
  N7: Raspberry_Pi1.GPIO_22, LED4.anode
  N8: Raspberry_Pi1.GPIO_4, LED1.anode
  N9: Raspberry_Pi1.GPIO_24, S3.COM
  N10: Raspberry_Pi1.GPIO_25, LED3.anode
  N11: LED1.cathode, LED2.cathode, LED3.cathode, LED4.cathode, R1.Pin_1, LED5.cathode, S3.L2

notes:
  The toggle switch used has a safety cover and led that lights when armed.
